// Logisim project alu.circ as structural Verilog: 1 circuit, main circuit alu
module alu (
  input  [31:0] A,
  input  [31:0] B,
  input  [3:0] ALUSel,
  output [31:0] Result
);

  wire adder_6_cout, comparator_1_eq, comparator_2_eq, comparator_3_eq, comparator_4_lt, or_1_out, xnor_1_out;
  wire [6:0] bitadder_1_out;
  wire [31:0] adder_2_out, adder_3_out, adder_4_out, adder_7_out, bit_extender_3_out, bit_extender_4_out,
       multiplexer_1_out, multiplexer_2_out, multiplier_2_cout, multiplier_3_out, multiplier_4_out,
       multiplier_5_cout, multiplier_5_out, not_1_out, not_2_out, not_3_out, not_4_out, result_add,
       result_and, result_bitpal, result_cnto, result_divu, result_mulh, result_mult, result_or, result_remu,
       result_sir, result_sll, result_slt, result_sra, result_srl, result_sub, result_xor;

  Comparator #(.width(32), .mode("unsigned")) comparator_1 (
    .a(A),
    .b({B[0], B[1], B[2], B[3], B[4], B[5], B[6], B[7], B[8], B[9], B[10], B[11], B[12], B[13], B[14], B[15], B[16], B[17], B[18], B[19], B[20], B[21], B[22], B[23], B[24], B[25], B[26], B[27], B[28], B[29], B[30], B[31]}),
    .eq(comparator_1_eq));  // open: gt, lt
  assign result_sir = {{31{1'b0}}, comparator_1_eq};  // Bit_Extender bit_extender_1
  Comparator #(.width(16), .mode("unsigned")) comparator_2 (
    .a({A[0], A[1], A[2], A[3], A[4], A[5], A[6], A[7], A[8], A[9], A[10], A[11], A[12], A[13], A[14], A[15]}),
    .b(A[31:16]), .eq(comparator_2_eq));  // open: gt, lt
  Comparator #(.width(16), .mode("unsigned")) comparator_3 (
    .a({B[0], B[1], B[2], B[3], B[4], B[5], B[6], B[7], B[8], B[9], B[10], B[11], B[12], B[13], B[14], B[15]}),
    .b(B[31:16]), .eq(comparator_3_eq));  // open: gt, lt
  or or_1 (or_1_out, comparator_2_eq, comparator_3_eq);
  assign result_bitpal = {{31{1'b0}}, or_1_out};  // Bit_Extender bit_extender_2
  Adder #(.width(32)) adder_1 (.a(A), .b(B), .out(result_add));  // open: cin, cout
  Subtractor #(.width(32)) subtractor_1 (.a(A), .b(B), .out(result_sub));  // open: bin, bout
  Multiplier #(.width(32)) multiplier_1 (.a(A), .b(B), .out(result_mult));  // open: cin, cout
  Divider #(.width(32)) divider_1 (.a(A), .b(B), .out(result_divu));  // open: upper, rem
  Divider #(.width(32)) divider_2 (.a(A), .b(B), .rem(result_remu));  // open: out, upper
  assign result_and = A & B;  // AND_Gate and_1, 32 bits wide
  assign result_or = A | B;  // OR_Gate or_2, 32 bits wide
  assign bit_extender_3_out = {{31{A[31]}}, A[31]};  // Bit_Extender bit_extender_3
  Multiplier #(.width(32)) multiplier_2 (.a(A), .b(B), .cout(multiplier_2_cout));  // open: out, cin
  assign bit_extender_4_out = {{31{B[31]}}, B[31]};  // Bit_Extender bit_extender_4
  Multiplier #(.width(32)) multiplier_3 (.a(bit_extender_3_out), .b(B), .out(multiplier_3_out));  // open: cin, cout
  Multiplier #(.width(32)) multiplier_4 (.a(A), .b(bit_extender_4_out), .out(multiplier_4_out));  // open: cin, cout
  assign not_1_out = ~A;  // NOT_Gate not_1, 32 bits wide
  assign not_2_out = ~B;  // NOT_Gate not_2, 32 bits wide
  Adder #(.width(32)) adder_2 (.a(multiplier_3_out), .b(multiplier_4_out), .out(adder_2_out));  // open: cin, cout
  Adder #(.width(32)) adder_3 (.a(not_1_out), .b(32'h1), .out(adder_3_out));  // open: cin, cout
  Adder #(.width(32)) adder_4 (.a(not_2_out), .b(32'h1), .out(adder_4_out));  // open: cin, cout
  Comparator #(.width(32)) comparator_4 (.a(A), .b(B), .lt(comparator_4_lt));  // open: gt, eq
  BitAdder #(.width(32)) bitadder_1 (.in0(A), .in1(B), .out(bitadder_1_out));
  Adder #(.width(32)) adder_5 (.a(multiplier_2_cout), .b(adder_2_out));  // open: out, cin, cout
  Multiplexer #(.width(32), .enable("false")) multiplexer_1 (
    .in0(A), .in1(adder_3_out), .out(multiplexer_1_out), .sel(A[31]));
  Multiplexer #(.width(32), .enable("false")) multiplexer_2 (
    .in0(B), .in1(adder_4_out), .out(multiplexer_2_out), .sel(B[31]));
  assign result_xor = A ^ B;  // XOR_Gate xor_1, 32 bits wide
  Shifter #(.width(32)) shifter_1 (.in(A), .\dist (B[4:0]), .out(result_sll));
  assign result_slt = {{31{1'b0}}, comparator_4_lt};  // Bit_Extender bit_extender_5
  Shifter #(.width(32), .shift("ar")) shifter_2 (.in(A), .\dist (B[4:0]), .out(result_sra));
  Shifter #(.width(32), .shift("lr")) shifter_3 (.in(A), .\dist (B[4:0]), .out(result_srl));
  assign result_cnto = {{25{1'b0}}, bitadder_1_out};  // Bit_Extender bit_extender_6
  Multiplier #(.width(32)) multiplier_5 (
    .a(multiplexer_1_out), .b(multiplexer_2_out), .out(multiplier_5_out), .cout(multiplier_5_cout));  // open: cin
  xnor xnor_1 (xnor_1_out, A[31], B[31]);
  assign not_3_out = ~multiplier_5_out;  // NOT_Gate not_3, 32 bits wide
  assign not_4_out = ~multiplier_5_cout;  // NOT_Gate not_4, 32 bits wide
  Adder #(.width(32)) adder_6 (.a(32'h1), .b(not_3_out), .cout(adder_6_cout));  // open: out, cin
  Adder #(.width(32)) adder_7 (.a({32{1'b0}}), .b(not_4_out), .out(adder_7_out), .cin(adder_6_cout));  // open: cout
  Multiplexer #(.width(32), .enable("false")) multiplexer_3 (
    .in0(adder_7_out), .in1(multiplier_5_cout), .out(result_mulh), .sel(xnor_1_out));
  Multiplexer #(.select(4), .width(32), .enable("false")) multiplexer_4 (
    .in0(result_add), .in1(result_sub), .in2(result_mulh), .in3(result_mult), .in4(result_divu),
    .in5(result_remu), .in6(result_and), .in7(result_or), .in8(result_xor), .in9(result_sll),
    .in10(result_slt), .in11(result_sra), .in12(result_srl), .in13(result_cnto), .in14(result_bitpal),
    .in15(result_sir), .out(Result), .sel(ALUSel));

  // Notes on the sheet:
  //   INPUTS to your circuit
  //   Arthmetic Operations
  //   Multiplexer
  //   OUTPUT from your circuit
endmodule
