// Logisim project cpu.circ as structural Verilog: 4 circuits, main circuit main
module main (
  input  [31:0] INSTRUCTION,
  input  CLOCK,
  output [31:0] FETCH_ADDRESS,
  output [31:0] ra,
  output [31:0] sp,
  output [31:0] t0,
  output [31:0] t1,
  output [31:0] t2,
  output [31:0] s0,
  output [31:0] s1,
  output [31:0] a0
);

  wire BrEq, BrLT, BrUn, BSel, MemRW, PCSel, RegWen;
  wire [1:0] ASel, WBSel;
  wire [2:0] DataSel, ImmSel;
  wire [3:0] ALUSel;
  wire [31:0] adder_1_out, ALUResult, bit_extender_1_out, bit_extender_2_out, bit_extender_3_out,
       bit_extender_4_out, DMEM_readdata, Imm, INST, MEMData, multiplexer_1_out, multiplexer_2_out,
       multiplexer_3_out, multiplexer_4_out, PCf, PCm, PCx, rs1, rs2, WriteData;

  Adder #(.width(32)) adder_1 (.a(PCf), .b(32'h4), .out(adder_1_out));  // open: cin, cout
  Multiplexer #(.width(32), .enable("false")) multiplexer_1 (
    .in0(adder_1_out), .in1(ALUResult), .out(multiplexer_1_out), .sel(PCSel));
  Register #(.width(32)) pcD (.D(PCf), .clk(CLOCK), .Q(PCx));  // open: en, clr
  Multiplexer #(.width(32), .enable("false")) multiplexer_2 (
    .in0(INSTRUCTION), .in1(32'h13), .out(multiplexer_2_out), .sel(PCSel));
  Register #(.width(32)) PC (.D(multiplexer_1_out), .clk(CLOCK), .Q(PCf));  // open: en, clr
  Register #(.width(32)) instD (.D(multiplexer_2_out), .clk(CLOCK), .Q(INST));  // open: en, clr
  Control control_1 (
    .Instruction(INST), .BrEq(BrEq), .BrLT(BrLT), .PCSel(PCSel), .ImmSel(ImmSel), .BrUn(BrUn), .ASel(ASel),
    .BSel(BSel), .ALUSel(ALUSel), .MemRW(MemRW), .RegWEn(RegWen), .WBSel(WBSel), .DataSel(DataSel));
  Shifter #(.width(32), .shift("lr")) shifter_1 (.in(PCf), .\dist (5'b00010), .out(FETCH_ADDRESS));
  Multiplexer #(.select(2), .width(32), .enable("false")) multiplexer_3 (
    .in0(rs1), .in1(PCx), .in2({32{1'b0}}), .out(multiplexer_3_out), .sel(ASel));  // open: in3
  Multiplexer #(.width(32), .enable("false")) multiplexer_4 (.in0(rs2), .in1(Imm), .out(multiplexer_4_out), .sel(BSel));
  ImmediateGen immediategen_1 (.Instruction(INST[31:7]), .ImmSel(ImmSel), .Immediate(Imm));
  alu alu_1 (.A(multiplexer_3_out), .B(multiplexer_4_out), .ALUSel(ALUSel), .Result(ALUResult));
  BranchCompare branchcompare_1 (.DataA(rs1), .DataB(rs2), .BrUn(BrUn), .BrEq(BrEq), .BrLT(BrLT));
  regfile_main RegFile (
    .rs2(INST[24:20]), .rd(INST[11:7]), .Read_Data_1(rs1), .Read_Data_2(rs2), .ra(ra), .sp(sp), .t0(t0),
    .t1(t1), .t2(t2), .s0(s0), .s1(s1), .a0(a0), .rs1(INST[19:15]), .Write_Data(WriteData), .RegWEn(RegWen),
    .clk(CLOCK));
  // Probe on PCSel
  // Probe on ImmSel
  // Probe on BrUn
  // Probe on ASel
  // Probe on BSel
  // Probe on ALUSel
  // Probe on MemRW
  // Probe on RegWen
  // Probe on WBSel
  // Probe on DataSel
  Multiplexer #(.select(2), .width(32), .enable("false")) multiplexer_5 (
    .in0(MEMData), .in1(ALUResult), .in2(PCm), .out(WriteData), .sel(WBSel));  // open: in3
  mem_main DMEM (.ReadData(DMEM_readdata), .WriteData(rs2), .clk(CLOCK), .WriteEN(MemRW), .ADDR(ALUResult));
  assign bit_extender_1_out = {{24{DMEM_readdata[7]}}, DMEM_readdata[7:0]};  // Bit_Extender bit_extender_1
  assign bit_extender_2_out = {{16{DMEM_readdata[15]}}, DMEM_readdata[15:0]};  // Bit_Extender bit_extender_2
  assign bit_extender_3_out = {{24{1'b0}}, DMEM_readdata[7:0]};  // Bit_Extender bit_extender_3
  assign bit_extender_4_out = {{16{1'b0}}, DMEM_readdata[15:0]};  // Bit_Extender bit_extender_4
  Adder #(.width(32)) adder_2 (.a(PCx), .b(32'h4), .out(PCm));  // open: cin, cout
  Multiplexer #(.select(3), .width(32), .enable("false")) multiplexer_6 (
    .in0(bit_extender_1_out), .in1(bit_extender_2_out), .in2(DMEM_readdata), .in3(bit_extender_3_out),
    .in4(bit_extender_4_out), .out(MEMData), .sel(DataSel));  // open: in5, in6, in7

  // Other names for the same wires on the sheet: clk = CLOCK; fetch_addr[31:0] = FETCH_ADDRESS;
  //   reg_rd[4:0] = INST[11:7]; reg_rs1[4:0] = INST[19:15]; reg_rs2[4:0] = INST[24:20]

  // Notes on the sheet:
  //   Output
  //   Instruction Fetch
  //   Intermediate Registers
  //   Control Logic
  //   Inputs/Outputs from run.circ. DO NOT MOVE THESE.
  //   Inputs
  //   Instruction Decode
  //   Execute
  //   Debug Output
  //   Inputs/Outputs from run.circ. DO NOT MOVE THESE.
  //   Memory
endmodule

module ImmediateGen (
  input  [24:0] Instruction,
  input  [2:0] ImmSel,
  output [31:0] Immediate
);

  wire [31:0] bit_extender_1_out, bit_extender_2_out, bit_extender_3_out, bit_extender_4_out;

  assign bit_extender_1_out = {{20{Instruction[24]}}, Instruction[24:13]};  // Bit_Extender bit_extender_1
  assign bit_extender_2_out = {{20{Instruction[24]}}, {Instruction[24:18], Instruction[4:0]}};  // Bit_Extender bit_extender_2
  assign bit_extender_3_out = {{19{Instruction[24]}}, {Instruction[24], Instruction[0], Instruction[23:18], Instruction[4:1], 1'b0}};  // Bit_Extender bit_extender_3
  assign bit_extender_4_out = {{11{Instruction[24]}}, {Instruction[24], Instruction[12:5], Instruction[13], Instruction[23:14], 1'b0}};  // Bit_Extender bit_extender_4
  Multiplexer #(.select(3), .width(32), .enable("false")) multiplexer_1 (
    .in0(bit_extender_1_out), .in1(bit_extender_2_out), .in2(bit_extender_3_out),
    .in3({Instruction[24:5], {12{1'b0}}}), .in4(bit_extender_4_out), .out(Immediate), .sel(ImmSel));  // open: in5, in6, in7

  // Notes on the sheet:
  //   I-imm
  //   S-imm
  //   B-imm
  //   U-imm
  //   J-imm
endmodule

module Control (
  input  [31:0] Instruction,
  input  BrEq,
  input  BrLT,
  output PCSel,
  output [2:0] ImmSel,
  output BrUn,
  output [1:0] ASel,
  output BSel,
  output [3:0] ALUSel,
  output MemRW,
  output RegWEn,
  output [1:0] WBSel,
  output [2:0] DataSel
);

  wire and_1_out, and_2_out, and_3_out, and_4_out, and_5_out, and_6_out, and_7_out, and_8_out, and_9_out,
       and_10_out, and_11_out, and_12_out, and_13_out, and_15_out, and_16_out, and_17_out, and_18_out,
       and_19_out, and_20_out, comparator_1_eq, comparator_2_eq, comparator_3_eq, comparator_4_eq,
       comparator_5_eq, comparator_6_eq, comparator_7_eq, comparator_8_eq, comparator_9_eq, comparator_10_eq,
       comparator_11_eq, comparator_12_eq, comparator_13_eq, comparator_14_eq, comparator_15_eq,
       comparator_16_eq, comparator_17_eq, comparator_18_eq, comparator_19_eq, comparator_20_eq,
       comparator_21_eq, comparator_22_eq, comparator_23_eq, comparator_24_eq, comparator_25_eq,
       comparator_26_eq, comparator_27_eq, comparator_28_eq, comparator_29_eq, comparator_30_eq,
       comparator_31_eq, comparator_32_eq, comparator_33_eq, comparator_34_eq, comparator_35_eq,
       comparator_36_eq, comparator_37_eq, comparator_38_eq, comparator_39_eq, I1type, I2type, I3type,
       or_1_out, or_2_out, or_3_out, or_4_out, or_5_out, or_6_out, or_8_out, or_9_out, Rtype, SBtype, U1type,
       U2type, UJtype;
  wire [1:0] multiplexer_17_out, multiplexer_25_out;
  wire [2:0] func3_out, multiplexer_20_out, multiplexer_21_out, multiplexer_22_out, multiplexer_23_out,
       multiplexer_24_out, multiplexer_27_out, multiplexer_28_out, multiplexer_29_out;
  wire [3:0] multiplexer_2_out, multiplexer_3_out, multiplexer_4_out, multiplexer_5_out, multiplexer_6_out,
       multiplexer_7_out, multiplexer_8_out, multiplexer_9_out, multiplexer_10_out, multiplexer_11_out,
       multiplexer_12_out, multiplexer_13_out, multiplexer_14_out;
  wire [6:0] func7_out;

  Multiplexer #(.width(7), .enable("false")) multiplexer_1 (
    .in0({7{1'b0}}), .in1(Instruction[31:25]), .out(func7_out), .sel(Rtype));
  Comparator #(.width(7), .mode("unsigned")) comparator_1 (
    .a(func7_out), .b(7'b0100000), .eq(comparator_1_eq));  // open: gt, lt
  Comparator #(.width(3), .mode("unsigned")) comparator_2 (
    .a(func3_out), .b(3'b000), .eq(comparator_2_eq));  // open: gt, lt
  Comparator #(.width(7), .mode("unsigned")) comparator_3 (
    .a(func7_out), .b(7'b0000001), .eq(comparator_3_eq));  // open: gt, lt
  Comparator #(.width(3), .mode("unsigned")) comparator_4 (
    .a(func3_out), .b(3'b001), .eq(comparator_4_eq));  // open: gt, lt
  or or_1 (or_1_out, comparator_4_eq, comparator_5_eq);
  Comparator #(.width(3), .mode("unsigned")) comparator_5 (
    .a(func3_out), .b(3'b011), .eq(comparator_5_eq));  // open: gt, lt
  Comparator #(.width(7), .mode("unsigned")) comparator_6 (
    .a(func7_out), .b(7'b0000001), .eq(comparator_6_eq));  // open: gt, lt
  Comparator #(.width(3), .mode("unsigned")) comparator_7 (
    .a(func3_out), .b(3'b000), .eq(comparator_7_eq));  // open: gt, lt
  Comparator #(.width(7), .mode("unsigned")) comparator_8 (
    .a(func7_out), .b(7'b0000001), .eq(comparator_8_eq));  // open: gt, lt
  Comparator #(.width(3), .mode("unsigned")) comparator_9 (
    .a(func3_out), .b(3'b101), .eq(comparator_9_eq));  // open: gt, lt
  Comparator #(.width(7), .mode("unsigned")) comparator_10 (
    .a(func7_out), .b(7'b0000001), .eq(comparator_10_eq));  // open: gt, lt
  Comparator #(.width(3), .mode("unsigned")) comparator_11 (
    .a(func3_out), .b(3'b111), .eq(comparator_11_eq));  // open: gt, lt
  Comparator #(.width(7), .mode("unsigned")) comparator_12 (
    .a(func7_out), .b({7{1'b0}}), .eq(comparator_12_eq));  // open: gt, lt
  Comparator #(.width(3), .mode("unsigned")) comparator_13 (
    .a(func3_out), .b(3'b111), .eq(comparator_13_eq));  // open: gt, lt
  Comparator #(.width(7), .mode("unsigned")) comparator_14 (
    .a(func7_out), .b({7{1'b0}}), .eq(comparator_14_eq));  // open: gt, lt
  Comparator #(.width(3), .mode("unsigned")) comparator_15 (
    .a(func3_out), .b(3'b110), .eq(comparator_15_eq));  // open: gt, lt
  Comparator #(.width(7), .mode("unsigned")) comparator_16 (
    .a(func7_out), .b({7{1'b0}}), .eq(comparator_16_eq));  // open: gt, lt
  Comparator #(.width(3), .mode("unsigned")) comparator_17 (
    .a(func3_out), .b(3'b100), .eq(comparator_17_eq));  // open: gt, lt
  Comparator #(.width(7), .mode("unsigned")) comparator_18 (
    .a(func7_out), .b({7{1'b0}}), .eq(comparator_18_eq));  // open: gt, lt
  Comparator #(.width(3), .mode("unsigned")) comparator_19 (
    .a(func3_out), .b(3'b001), .eq(comparator_19_eq));  // open: gt, lt
  Comparator #(.width(7), .mode("unsigned")) comparator_20 (
    .a(func7_out), .b({7{1'b0}}), .eq(comparator_20_eq));  // open: gt, lt
  Comparator #(.width(3), .mode("unsigned")) comparator_21 (
    .a(func3_out), .b(3'b010), .eq(comparator_21_eq));  // open: gt, lt
  Comparator #(.width(7), .mode("unsigned")) comparator_22 (
    .a(func7_out), .b(7'b0100000), .eq(comparator_22_eq));  // open: gt, lt
  Comparator #(.width(3), .mode("unsigned")) comparator_23 (
    .a(func3_out), .b(3'b101), .eq(comparator_23_eq));  // open: gt, lt
  Comparator #(.width(7), .mode("unsigned")) comparator_24 (
    .a(func7_out), .b({7{1'b0}}), .eq(comparator_24_eq));  // open: gt, lt
  Comparator #(.width(3), .mode("unsigned")) comparator_25 (
    .a(func3_out), .b(3'b101), .eq(comparator_25_eq));  // open: gt, lt
  Comparator #(.width(7), .mode("unsigned")) comparator_26 (
    .a(func7_out), .b({7{1'b0}}), .eq(comparator_26_eq));  // open: gt, lt
  Comparator #(.width(3), .mode("unsigned")) comparator_27 (
    .a(func3_out), .b(3'b011), .eq(comparator_27_eq));  // open: gt, lt
  and and_1 (and_1_out, comparator_1_eq, comparator_2_eq);
  Multiplexer #(.width(4), .enable("false")) multiplexer_2 (
    .in0(4'b0000), .in1(4'b0001), .out(multiplexer_2_out), .sel(and_1_out));
  and and_2 (and_2_out, comparator_3_eq, or_1_out);
  Multiplexer #(.width(4), .enable("false")) multiplexer_3 (
    .in0(multiplexer_2_out), .in1(4'b0010), .out(multiplexer_3_out), .sel(and_2_out));
  and and_3 (and_3_out, comparator_6_eq, comparator_7_eq);
  Multiplexer #(.width(4), .enable("false")) multiplexer_4 (
    .in0(multiplexer_3_out), .in1(4'b0011), .out(multiplexer_4_out), .sel(and_3_out));
  and and_4 (and_4_out, comparator_8_eq, comparator_9_eq);
  Multiplexer #(.width(4), .enable("false")) multiplexer_5 (
    .in0(multiplexer_4_out), .in1(4'b0100), .out(multiplexer_5_out), .sel(and_4_out));
  and and_5 (and_5_out, comparator_10_eq, comparator_11_eq);
  Multiplexer #(.width(4), .enable("false")) multiplexer_6 (
    .in0(multiplexer_5_out), .in1(4'b0101), .out(multiplexer_6_out), .sel(and_5_out));
  and and_6 (and_6_out, comparator_12_eq, comparator_13_eq);
  Multiplexer #(.width(4), .enable("false")) multiplexer_7 (
    .in0(multiplexer_6_out), .in1(4'b0110), .out(multiplexer_7_out), .sel(and_6_out));
  and and_7 (and_7_out, comparator_14_eq, comparator_15_eq);
  Multiplexer #(.width(4), .enable("false")) multiplexer_8 (
    .in0(multiplexer_7_out), .in1(4'b0111), .out(multiplexer_8_out), .sel(and_7_out));
  and and_8 (and_8_out, comparator_16_eq, comparator_17_eq);
  Multiplexer #(.width(4), .enable("false")) multiplexer_9 (
    .in0(multiplexer_8_out), .in1(4'b1000), .out(multiplexer_9_out), .sel(and_8_out));
  and and_9 (and_9_out, comparator_18_eq, comparator_19_eq);
  Multiplexer #(.width(4), .enable("false")) multiplexer_10 (
    .in0(multiplexer_9_out), .in1(4'b1001), .out(multiplexer_10_out), .sel(and_9_out));
  and and_10 (and_10_out, comparator_20_eq, comparator_21_eq);
  Multiplexer #(.width(4), .enable("false")) multiplexer_11 (
    .in0(multiplexer_10_out), .in1(4'b1010), .out(multiplexer_11_out), .sel(and_10_out));
  and and_11 (and_11_out, comparator_22_eq, comparator_23_eq);
  Multiplexer #(.width(4), .enable("false")) multiplexer_12 (
    .in0(multiplexer_11_out), .in1(4'b1011), .out(multiplexer_12_out), .sel(and_11_out));
  and and_12 (and_12_out, comparator_24_eq, comparator_25_eq);
  Multiplexer #(.width(4), .enable("false")) multiplexer_13 (
    .in0(multiplexer_12_out), .in1(4'b1100), .out(multiplexer_13_out), .sel(and_12_out));
  and and_13 (and_13_out, comparator_26_eq, comparator_27_eq);
  Multiplexer #(.width(4), .enable("false")) multiplexer_14 (
    .in0(multiplexer_13_out), .in1(4'b1101), .out(multiplexer_14_out), .sel(and_13_out));
  or or_2 (or_2_out, Rtype, I2type);
  Multiplexer #(.width(4), .enable("false")) multiplexer_15 (
    .in0(4'b0000), .in1(multiplexer_14_out), .out(ALUSel), .sel(or_2_out));
  Multiplexer #(.width(3), .enable("false")) multiplexer_16 (
    .in0(Instruction[14:12]), .in1(3'b000), .out(func3_out), .sel(or_3_out));
  or or_3 (or_3_out, U1type, U2type, UJtype);
  Comparator #(.width(3), .mode("unsigned")) comparator_28 (
    .a(Instruction[14:12]), .b(3'b000), .eq(comparator_28_eq));  // open: gt, lt
  Comparator #(.width(3), .mode("unsigned")) comparator_29 (
    .a(Instruction[14:12]), .b(3'b100), .eq(comparator_29_eq));  // open: gt, lt
  Comparator #(.width(3), .mode("unsigned")) comparator_30 (
    .a(Instruction[14:12]), .b(3'b110), .eq(comparator_30_eq));  // open: gt, lt
  Comparator #(.width(3), .mode("unsigned")) comparator_31 (
    .a(Instruction[14:12]), .b(3'b001), .eq(comparator_31_eq));  // open: gt, lt
  Comparator #(.width(3), .mode("unsigned")) comparator_32 (
    .a(Instruction[14:12]), .b(3'b111), .eq(comparator_32_eq));  // open: gt, lt
  Comparator #(.width(3), .mode("unsigned")) comparator_33 (
    .a(Instruction[14:12]), .b(3'b110), .eq(comparator_33_eq));  // open: gt, lt
  Comparator #(.width(3), .mode("unsigned")) comparator_34 (
    .a(Instruction[14:12]), .b(3'b111), .eq(comparator_34_eq));  // open: gt, lt
  nor nor_1 (RegWEn, MemRW, SBtype);
  Multiplexer #(.width(2), .enable("false")) multiplexer_17 (
    .in0(2'b01), .in1(2'b00), .out(multiplexer_17_out), .sel(I1type));
  or or_4 (or_4_out, UJtype, I3type);
  Multiplexer #(.width(2), .enable("false")) multiplexer_18 (
    .in0(multiplexer_17_out), .in1(2'b10), .out(WBSel), .sel(or_4_out));
  or or_5 (or_5_out, comparator_33_eq, comparator_34_eq);
  and and_14 (BrUn, or_5_out, SBtype);
  and and_15 (and_15_out, BrEq, comparator_28_eq);
  and and_16 (and_16_out, BrLT, comparator_29_eq);
  and and_17 (and_17_out, BrLT, comparator_30_eq);
  and and_18 (and_18_out, ~BrEq, comparator_31_eq);  // AND_Gate
  and and_19 (and_19_out, ~BrLT, comparator_32_eq);  // AND_Gate
  and and_20 (and_20_out, SBtype, or_6_out);
  or or_6 (or_6_out, and_15_out, and_16_out, and_17_out, and_18_out, and_19_out);
  Multiplexer #(.width(3), .enable("false")) multiplexer_19 (
    .in0(3'b010), .in1(multiplexer_24_out), .out(DataSel), .sel(I1type));
  or or_7 (PCSel, and_20_out, UJtype, I3type);
  Comparator #(.width(3), .mode("unsigned")) comparator_35 (
    .a(Instruction[14:12]), .b(3'b000), .eq(comparator_35_eq));  // open: gt, lt
  Multiplexer #(.width(3), .enable("false")) multiplexer_20 (
    .in0(3'b010), .in1(3'b000), .out(multiplexer_20_out), .sel(comparator_35_eq));
  Comparator #(.width(3), .mode("unsigned")) comparator_36 (
    .a(Instruction[14:12]), .b(3'b001), .eq(comparator_36_eq));  // open: gt, lt
  Multiplexer #(.width(3), .enable("false")) multiplexer_21 (
    .in0(multiplexer_20_out), .in1(3'b001), .out(multiplexer_21_out), .sel(comparator_36_eq));
  Comparator #(.width(3), .mode("unsigned")) comparator_37 (
    .a(Instruction[14:12]), .b(3'b010), .eq(comparator_37_eq));  // open: gt, lt
  Multiplexer #(.width(3), .enable("false")) multiplexer_22 (
    .in0(multiplexer_21_out), .in1(3'b010), .out(multiplexer_22_out), .sel(comparator_37_eq));
  Comparator #(.width(3), .mode("unsigned")) comparator_38 (
    .a(Instruction[14:12]), .b(3'b100), .eq(comparator_38_eq));  // open: gt, lt
  Multiplexer #(.width(3), .enable("false")) multiplexer_23 (
    .in0(multiplexer_22_out), .in1(3'b011), .out(multiplexer_23_out), .sel(comparator_38_eq));
  Comparator #(.width(3), .mode("unsigned")) comparator_39 (
    .a(Instruction[14:12]), .b(3'b101), .eq(comparator_39_eq));  // open: gt, lt
  Multiplexer #(.width(3), .enable("false")) multiplexer_24 (
    .in0(multiplexer_23_out), .in1(3'b100), .out(multiplexer_24_out), .sel(comparator_39_eq));
  Multiplexer #(.width(2), .enable("false")) multiplexer_25 (
    .in0(2'b00), .in1(2'b01), .out(multiplexer_25_out), .sel(or_8_out));
  or or_8 (or_8_out, SBtype, UJtype, U1type);
  Multiplexer #(.width(2), .enable("false")) multiplexer_26 (
    .in0(multiplexer_25_out), .in1(2'b10), .out(ASel), .sel(U2type));
  Multiplexer #(.width(3), .enable("false")) multiplexer_27 (
    .in0(3'b000), .in1(3'b001), .out(multiplexer_27_out), .sel(MemRW));
  Multiplexer #(.width(3), .enable("false")) multiplexer_28 (
    .in0(multiplexer_27_out), .in1(3'b010), .out(multiplexer_28_out), .sel(SBtype));
  or or_9 (or_9_out, U1type, U2type);
  Multiplexer #(.width(3), .enable("false")) multiplexer_29 (
    .in0(multiplexer_28_out), .in1(3'b011), .out(multiplexer_29_out), .sel(or_9_out));
  Multiplexer #(.width(3), .enable("false")) multiplexer_30 (
    .in0(multiplexer_29_out), .in1(3'b100), .out(ImmSel), .sel(UJtype));
  not not_1 (BSel, Rtype);
  Comparator #(.width(7), .mode("unsigned")) comparator_40 (
    .a(Instruction[6:0]), .b(7'b0110011), .eq(Rtype));  // open: gt, lt
  Comparator #(.width(7), .mode("unsigned")) comparator_41 (
    .a(Instruction[6:0]), .b(7'b0000011), .eq(I1type));  // open: gt, lt
  Comparator #(.width(7), .mode("unsigned")) comparator_42 (
    .a(Instruction[6:0]), .b(7'b0010011), .eq(I2type));  // open: gt, lt
  Comparator #(.width(7), .mode("unsigned")) comparator_43 (
    .a(Instruction[6:0]), .b(7'b0100011), .eq(MemRW));  // open: gt, lt
  Comparator #(.width(7), .mode("unsigned")) comparator_44 (
    .a(Instruction[6:0]), .b(7'b1100011), .eq(SBtype));  // open: gt, lt
  Comparator #(.width(7), .mode("unsigned")) comparator_45 (
    .a(Instruction[6:0]), .b(7'b0010111), .eq(U1type));  // open: gt, lt
  Comparator #(.width(7), .mode("unsigned")) comparator_46 (
    .a(Instruction[6:0]), .b(7'b0110111), .eq(U2type));  // open: gt, lt
  Comparator #(.width(7), .mode("unsigned")) comparator_47 (
    .a(Instruction[6:0]), .b(7'b1101111), .eq(UJtype));  // open: gt, lt
  Comparator #(.width(7), .mode("unsigned")) comparator_48 (
    .a(Instruction[6:0]), .b(7'b1100111), .eq(I3type));  // open: gt, lt

  // Other names for the same wires on the sheet: opcode[6:0] = Instruction[6:0]; func3[2:0] = Instruction[14:12];
  //   func7[6:0] = Instruction[31:25]; Stype = MemRW

  // Notes on the sheet:
  //   ALUSel
  //   sll
  //   slt
  //   sra
  //   sub
  //   mulh
  //   mult
  //   divu
  //   remu
  //   and
  //   or
  //   xor
  //   srl
  //   sltu
  //   MenRW
  //   BrUn
  //   RegWEn
  //   WBSel
  //   Input
  //   PCSel
  //   ASel
  //   DataSel
  //   Output
  //   ImmSel
  //   Type
  //   BSel
endmodule

module BranchCompare (
  input  [31:0] DataA,
  input  [31:0] DataB,
  input  BrUn,
  output BrEq,
  output BrLT
);

  wire comparator_1_eq, comparator_1_lt, comparator_2_eq, comparator_2_lt;

  Comparator #(.width(32)) comparator_1 (.a(DataA), .b(DataB), .eq(comparator_1_eq), .lt(comparator_1_lt));  // open: gt
  Comparator #(.width(32), .mode("unsigned")) comparator_2 (
    .a(DataA), .b(DataB), .eq(comparator_2_eq), .lt(comparator_2_lt));  // open: gt
  Multiplexer #(.enable("false")) multiplexer_1 (.in0(comparator_1_eq), .in1(comparator_2_eq), .out(BrEq), .sel(BrUn));
  Multiplexer #(.enable("false")) multiplexer_2 (.in0(comparator_1_lt), .in1(comparator_2_lt), .out(BrLT), .sel(BrUn));
endmodule
