// Logisim project mem.circ as structural Verilog: 1 circuit, main circuit main
module main (
  input  [31:0] ADDR,
  input  WriteEN,
  input  clk,
  input  [31:0] WriteData,
  output [31:0] ReadData
);

  RAM #(.addrWidth(14), .dataWidth(32), .trigger("falling"), .databus("bibus")) DMEM (
    .addr(ADDR[13:0]), .we(WriteEN), .oe(1'b1), .clk(clk), .din(WriteData), .dout(ReadData));

  // Notes on the sheet:
  //   bottom 14 bit of addr
endmodule
