// Logisim project alu.circ as structural Verilog: 1 circuit, main circuit alu
module alu (
  input  [31:0] A,
  input  [31:0] B,
  input  [3:0] ALUSel,
  output [31:0] Result
);

  wire adder_4_cout, comparator_1_eq, comparator_2_lt, comparator_3_lt, xnor_1_out;
  wire [6:0] bitadder_1_out;
  wire [31:0] adder_2_out, adder_3_out, adder_5_out, divider_2_rem, multiplexer_2_out, multiplexer_3_out,
       multiplier_2_cout, multiplier_2_out, not_1_out, not_2_out, not_3_out, not_4_out, result_add,
       result_and, result_cnto, result_divu, result_mulh, result_mult, result_or, result_remu, result_sll,
       result_slt, result_sltu, result_sra, result_srl, result_sub, result_xor;

  Adder #(.width(32)) adder_1 (.a(A), .b(B), .out(result_add));  // open: cin, cout
  Subtractor #(.width(32)) subtractor_1 (.a(A), .b(B), .out(result_sub));  // open: bin, bout
  Multiplier #(.width(32)) multiplier_1 (.a(A), .b(B), .out(result_mult));  // open: cin, cout
  Divider #(.width(32)) divider_1 (.a(A), .b(B), .out(result_divu));  // open: upper, rem
  assign result_and = A & B;  // AND_Gate and_1, 32 bits wide
  assign result_or = A | B;  // OR_Gate or_1, 32 bits wide
  Divider #(.width(32)) divider_2 (.a(A), .b(B), .rem(divider_2_rem));  // open: out, upper
  Multiplexer #(.width(32), .enable("false")) multiplexer_1 (
    .in0(divider_2_rem), .in1(A), .out(result_remu), .sel(comparator_1_eq));
  Comparator #(.width(32), .mode("unsigned")) comparator_1 (
    .a(B), .b({32{1'b0}}), .eq(comparator_1_eq));  // open: gt, lt
  assign not_1_out = ~A;  // NOT_Gate not_1, 32 bits wide
  Adder #(.width(32)) adder_2 (.a(not_1_out), .b(32'h1), .out(adder_2_out));  // open: cin, cout
  assign not_2_out = ~B;  // NOT_Gate not_2, 32 bits wide
  Adder #(.width(32)) adder_3 (.a(not_2_out), .b(32'h1), .out(adder_3_out));  // open: cin, cout
  Multiplexer #(.width(32), .enable("false")) multiplexer_2 (
    .in0(A), .in1(adder_2_out), .out(multiplexer_2_out), .sel(A[31]));
  Multiplexer #(.width(32), .enable("false")) multiplexer_3 (
    .in0(B), .in1(adder_3_out), .out(multiplexer_3_out), .sel(B[31]));
  Multiplier #(.width(32)) multiplier_2 (
    .a(multiplexer_2_out), .b(multiplexer_3_out), .out(multiplier_2_out), .cout(multiplier_2_cout));  // open: cin
  xnor xnor_1 (xnor_1_out, A[31], B[31]);
  Comparator #(.width(32)) comparator_2 (.a(A), .b(B), .lt(comparator_2_lt));  // open: gt, eq
  BitAdder #(.width(32)) bitadder_1 (.in0(A), .in1(B), .out(bitadder_1_out));
  Comparator #(.width(32), .mode("unsigned")) comparator_3 (.a(A), .b(B), .lt(comparator_3_lt));  // open: gt, eq
  assign not_3_out = ~multiplier_2_out;  // NOT_Gate not_3, 32 bits wide
  assign not_4_out = ~multiplier_2_cout;  // NOT_Gate not_4, 32 bits wide
  assign result_xor = A ^ B;  // XOR_Gate xor_1, 32 bits wide
  Shifter #(.width(32)) shifter_1 (.in(A), .\dist (B[4:0]), .out(result_sll));
  assign result_slt = {{31{1'b0}}, comparator_2_lt};  // Bit_Extender bit_extender_1
  Shifter #(.width(32), .shift("ar")) shifter_2 (.in(A), .\dist (B[4:0]), .out(result_sra));
  Shifter #(.width(32), .shift("lr")) shifter_3 (.in(A), .\dist (B[4:0]), .out(result_srl));
  assign result_cnto = {{25{1'b0}}, bitadder_1_out};  // Bit_Extender bit_extender_2
  assign result_sltu = {{31{1'b0}}, comparator_3_lt};  // Bit_Extender bit_extender_3
  Adder #(.width(32)) adder_4 (.a(32'h1), .b(not_3_out), .cout(adder_4_cout));  // open: out, cin
  Adder #(.width(32)) adder_5 (.a({32{1'b0}}), .b(not_4_out), .out(adder_5_out), .cin(adder_4_cout));  // open: cout
  Multiplexer #(.width(32), .enable("false")) multiplexer_4 (
    .in0(adder_5_out), .in1(multiplier_2_cout), .out(result_mulh), .sel(xnor_1_out));
  Multiplexer #(.select(4), .width(32), .enable("false")) multiplexer_5 (
    .in0(result_add), .in1(result_sub), .in2(result_mulh), .in3(result_mult), .in4(result_divu),
    .in5(result_remu), .in6(result_and), .in7(result_or), .in8(result_xor), .in9(result_sll),
    .in10(result_slt), .in11(result_sra), .in12(result_srl), .in13(result_sltu), .out(Result), .sel(ALUSel));  // open: in14, in15

  // Notes on the sheet:
  //   INPUTS to your circuit
  //   Arthmetic Operations
  //   Multiplexer
  //   OUTPUT from your circuit
endmodule
